// Logisim project Artemis with 74ls181 ALU Logisim.circ as structural Verilog: 2 circuits, main circuit main
module main (
  input  [7:0] in_1,
  input  Data_In,
  input  Clear
);

  wire and_1_out, clock_1_out, decoder_1_out1, decoder_1_out2, decoder_1_out3, decoder_1_out4,
       decoder_1_out5, decoder_1_out6, decoder_1_out7, decoder_2_out1, decoder_2_out2, decoder_2_out3,
       decoder_2_out4, decoder_2_out5, decoder_2_out6, decoder_2_out7, decoder_3_out0, decoder_3_out1,
       decoder_3_out2, decoder_3_out3, decoder_3_out4, decoder_3_out5, decoder_3_out6, decoder_3_out7,
       decoder_3_out8, decoder_3_out9, not_1_out, not_2_out, not_3_out, or_1_out;
  wire [2:0] counter_1_q;
  wire [3:0] rom_2_data_2;
  wire [7:0] controlled_buffer_1_out, controlled_buffer_4_out, Flags_Register_q, Instruction_Register_q,
       Instruction_Register_q_2, Memory_Address_Register_q, Program_Counter_q, Reg_A_q, Reg_B_q, Reg_C_q,
       Reg_In_q, Reg_Out_q, Reg_Temp_q, rom_3_data, rom_4_data, Stack_Pointer_q, undriven;
  wire [7:4] rom_2_data;
  wire [15:0] rom_1_data;

  // Probe on Flags_Register_q[1:0]
  // Probe on counter_1_q
  Counter #(.width(3), .max('h7)) counter_1 (
    .Q(counter_1_q), .clk(not_1_out), .clr(or_1_out));  // open: load, D, count, carry
  not not_1 (not_1_out, and_1_out);
  // Probe on Instruction_Register_q_2
  Register Reg_In (.D(in_1), .en(Data_In), .Q(Reg_In_q), .clk(and_1_out), .clr(Clear));
  Counter Program_Counter (
    .load(rom_2_data[6]), .D(controlled_buffer_1_out), .count(rom_2_data[5]), .Q(Program_Counter_q),
    .clk(and_1_out), .clr(Clear));  // open: carry
  Register Memory_Address_Register (
    .D(controlled_buffer_1_out), .en(rom_4_data[0]), .Q(Memory_Address_Register_q), .clk(and_1_out),
    .clr(Clear));
  not not_2 (not_2_out, Memory_Address_Register_q[7]);
  Register #(.width(16)) Instruction_Register (
    .D({controlled_buffer_4_out, controlled_buffer_1_out}), .en(decoder_2_out6),
    .Q({Instruction_Register_q_2, Instruction_Register_q}), .clk(and_1_out), .clr(Clear));
  or or_1 (or_1_out, Clear, rom_2_data[4]);
  assign controlled_buffer_1_out = decoder_1_out5 ? Reg_In_q : 8'bz;  // Controlled_Buffer controlled_buffer_1
  assign controlled_buffer_1_out = rom_2_data[7] ? Program_Counter_q : 8'bz;  // Controlled_Buffer controlled_buffer_2
  ROM #(.dataWidth(16)) rom_1 (.addr(Memory_Address_Register_q), .data(rom_1_data), .sel(not_2_out));
  RAM #(.dataWidth(16)) ram_1 (
    .addr(Memory_Address_Register_q), .data(rom_1_data), .sel(Memory_Address_Register_q[7]), .clk(and_1_out),
    .ld(rom_3_data[0]), .clr(Clear));
  assign controlled_buffer_1_out = decoder_1_out6 ? Instruction_Register_q : 8'bz;  // Controlled_Buffer controlled_buffer_3
  Clock clock_1 (.out(clock_1_out));
  ROM #(.addrWidth(13)) rom_2 (
    .addr({Flags_Register_q[1:0], counter_1_q, Instruction_Register_q_2}), .data({rom_2_data, rom_2_data_2}));  // open: sel
  ROM #(.addrWidth(13)) rom_3 (
    .addr({Flags_Register_q[1:0], counter_1_q, Instruction_Register_q_2}), .data(rom_3_data));  // open: sel
  ROM #(.addrWidth(13)) rom_4 (
    .addr({Flags_Register_q[1:0], counter_1_q, Instruction_Register_q_2}), .data(rom_4_data));  // open: sel
  assign {controlled_buffer_4_out, controlled_buffer_1_out} = rom_3_data[0] ? rom_1_data : 16'bz;  // Controlled_Buffer controlled_buffer_4
  assign rom_1_data = rom_3_data[4] ? {controlled_buffer_4_out, controlled_buffer_1_out} : 16'bz;  // Controlled_Buffer controlled_buffer_5
  and and_1 (and_1_out, clock_1_out, ~rom_4_data[2]);  // AND_Gate
  // Probe on {controlled_buffer_4_out, controlled_buffer_1_out}
  // Probe on {controlled_buffer_4_out, controlled_buffer_1_out}
  Pull_Resistor pull_resistor_1 (.node({controlled_buffer_4_out, controlled_buffer_1_out}));
  assign controlled_buffer_1_out = decoder_1_out1 ? Reg_A_q : 8'bz;  // Controlled_Buffer controlled_buffer_6
  Register Reg_A (.D(controlled_buffer_1_out), .en(decoder_2_out1), .Q(Reg_A_q), .clk(and_1_out), .clr(Clear));
  assign controlled_buffer_1_out = decoder_1_out2 ? Reg_Temp_q : 8'bz;  // Controlled_Buffer controlled_buffer_7
  Register Reg_Temp (.D(controlled_buffer_1_out), .en(decoder_2_out2), .Q(Reg_Temp_q), .clk(and_1_out), .clr(Clear));
  assign controlled_buffer_1_out = decoder_1_out3 ? Reg_B_q : 8'bz;  // Controlled_Buffer controlled_buffer_8
  Register Reg_B (.D(controlled_buffer_1_out), .en(decoder_2_out3), .Q(Reg_B_q), .clk(and_1_out), .clr(Clear));
  assign controlled_buffer_1_out = decoder_1_out4 ? Reg_C_q : 8'bz;  // Controlled_Buffer controlled_buffer_9
  Register Reg_C (.D(controlled_buffer_1_out), .en(decoder_2_out4), .Q(Reg_C_q), .clk(and_1_out), .clr(Clear));
  assign controlled_buffer_1_out = decoder_1_out7 ? Stack_Pointer_q : 8'bz;  // Controlled_Buffer controlled_buffer_10
  Register Stack_Pointer (
    .D(controlled_buffer_1_out), .en(decoder_2_out7), .Q(Stack_Pointer_q), .clk(and_1_out), .clr(Clear));
  Register Reg_Out (.D(controlled_buffer_1_out), .en(decoder_2_out5), .Q(Reg_Out_q), .clk(and_1_out), .clr(Clear));
  // Probe on Reg_Out_q
  Decoder #(.select(3), .enable("false")) decoder_1 (
    .out1(decoder_1_out1), .out2(decoder_1_out2), .out3(decoder_1_out3), .out4(decoder_1_out4),
    .out5(decoder_1_out5), .out6(decoder_1_out6), .out7(decoder_1_out7), .sel(rom_3_data[3:1]));  // open: out0
  not not_3 (not_3_out, decoder_3_out0);
  Decoder #(.select(3), .enable("false")) decoder_2 (
    .out1(decoder_2_out1), .out2(decoder_2_out2), .out3(decoder_2_out3), .out4(decoder_2_out4),
    .out5(decoder_2_out5), .out6(decoder_2_out6), .out7(decoder_2_out7), .sel(rom_3_data[7:5]));  // open: out0
  Register Flags_Register (.D(undriven), .en(rom_4_data[1]), .Q(Flags_Register_q), .clk(and_1_out), .clr(Clear));
  Decoder #(.select(4), .enable("false")) decoder_3 (
    .out0(decoder_3_out0), .out1(decoder_3_out1), .out2(decoder_3_out2), .out3(decoder_3_out3),
    .out4(decoder_3_out4), .out5(decoder_3_out5), .out6(decoder_3_out6), .out7(decoder_3_out7),
    .out8(decoder_3_out8), .out9(decoder_3_out9), .sel(rom_2_data_2));  // open: out10, out11, out12, out13, out14, out15

  // Notes on the sheet:
  //   Microcode Counter
  //   Microcode ROMs
  //   First 1/2 Memory ROM
  //   contents of rom_1 (hex, n*v repeats v):
  //   10e 20f 300 400 10*0 6 3
  //   ALU Control Word
  //   contents of rom_2 (hex, n*v repeats v):
  //   256*80 256*20 259*0 10 253*0 10 1 255*0 10
  //   contents of rom_3 (hex, n*v repeats v):
  //   256*0 256*c1 0 c c a2 253*0 21 41 255*0 20
  //   contents of rom_4 (hex, n*v repeats v):
  //   256*1 257*0 1 1 0 4
  //   Reg Out
  //   Reg In
  //   Halt
  //   Microcode Early Exit
  //   Top -> Bottom: Count Enable, In ,Out
  //   Reg A
  //   Reg T
  //   Reg B
  //   Reg C
  //   Reg I/O
  //   Instruction Register
  //   Stack Pointer
  //   Memory Address Reg + Reg F (Both load signals)
  //   Program Counter
  //   Program Memory
endmodule

module ALU (
  input  [4:0] Control_Word,
  input  [7:0] A_Input,
  input  [7:0] B_Input,
  output Zero_Flag,
  output [7:0] F_Output
);

  wire _74ls181_2_cn_4;

  _74181 _74ls181 (
    .S3(Control_Word[3]), .S2(Control_Word[2]), .S1(Control_Word[1]), .S0(Control_Word[0]), .B3(B_Input[7]),
    .A3(A_Input[7]), .B2(B_Input[6]), .A2(A_Input[6]), .B1(B_Input[5]), .A1(A_Input[5]), .B0(B_Input[4]),
    .A0(A_Input[4]), .M(Control_Word[4]), .Cn(_74ls181_2_cn_4), .F3(F_Output[7]), .F2(F_Output[6]),
    .F1(F_Output[5]), .F0(F_Output[4]));  // open: G, Cn_4, P, A_B
  _74181 _74ls181_2 (
    .S3(Control_Word[3]), .S2(Control_Word[2]), .S1(Control_Word[1]), .S0(Control_Word[0]), .B3(B_Input[3]),
    .A3(A_Input[3]), .B2(B_Input[2]), .A2(A_Input[2]), .B1(B_Input[1]), .A1(A_Input[1]), .B0(B_Input[0]),
    .A0(A_Input[0]), .M(Control_Word[4]), .Cn(1'b1), .Cn_4(_74ls181_2_cn_4), .F3(F_Output[3]),
    .F2(F_Output[2]), .F1(F_Output[1]), .F0(F_Output[0]));  // open: G, P, A_B
  nand nand_1 (Zero_Flag, F_Output[7], F_Output[6], F_Output[5], F_Output[4], F_Output[3], F_Output[2], F_Output[1], F_Output[0]);
endmodule
