// Logisim project SAP-3 Logisim.circ as structural Verilog: 4 circuits, main circuit main
module main (
  input  Reg_In_Out,
  input  [7:0] in_2,
  input  Input_Data,
  input  Reg_F_Load,
  input  Reg_A_Out,
  input  PC_Count_Enable,
  input  Reg_A_Load,
  input  PC_Load,
  input  Clear,
  input  PC_Out,
  input  MAR_Load,
  input  [3:0] ALU_Control_Word,
  input  IR_Load,
  input  IR_Out,
  input  Reg_Temp_Out,
  input  Reg_Temp_Load,
  input  Memory_Out,
  input  Memory_In,
  input  Reg_B_Out,
  input  Reg_B_Load,
  input  Reg_C_Out,
  input  Reg_C_Load,
  input  SP_Out,
  input  SP_Load,
  input  Reg_Out_Load
);

  wire CLK_out, decoder_2_out0, decoder_2_out1, decoder_2_out2, decoder_2_out3, decoder_2_out4,
       decoder_2_out5, decoder_2_out6, decoder_2_out7, decoder_2_out8, decoder_2_out9, not_1_out, not_2_out,
       not_3_out;
  wire [2:0] counter_1_q;
  wire [7:0] controlled_buffer_1_out, controlled_buffer_4_out, Instruction_Register_q,
       Instruction_Register_q_2, Memory_Address_Register_q, n8_bit_alu_1_carry_borrow_flag,
       Program_Counter_q, Reg_A_q, Reg_B_q, Reg_C_q, Reg_In_q, Reg_Out_q, Reg_Temp_q, rom_2_data,
       Stack_Pointer_q;
  wire [15:0] rom_1_data;

  Counter #(.width(3), .max('h7)) counter_1 (
    .load(1'b0), .D(3'b000), .count(1'b1), .Q(counter_1_q), .clk(not_1_out), .clr(Clear));  // open: carry
  not not_1 (not_1_out, CLK_out);
  Decoder #(.select(3), .enable("false")) decoder_1 (.sel(counter_1_q));  // open: out0, out1, out2, out3, out4, out5, out6, out7
  Register Reg_In (.D(in_2), .en(Input_Data), .Q(Reg_In_q), .clk(CLK_out), .clr(Clear));
  Counter Program_Counter (
    .load(PC_Load), .D(controlled_buffer_1_out), .count(PC_Count_Enable), .Q(Program_Counter_q),
    .clk(CLK_out), .clr(Clear));  // open: carry
  Register Memory_Address_Register (
    .D(controlled_buffer_1_out), .en(MAR_Load), .Q(Memory_Address_Register_q), .clk(CLK_out), .clr(Clear));
  not not_2 (not_2_out, Memory_Address_Register_q[7]);
  Register #(.width(16)) Instruction_Register (
    .D({controlled_buffer_4_out, controlled_buffer_1_out}), .en(IR_Load),
    .Q({Instruction_Register_q_2, Instruction_Register_q}), .clk(CLK_out), .clr(Clear));
  assign controlled_buffer_1_out = Reg_In_Out ? Reg_In_q : 8'bz;  // Controlled_Buffer controlled_buffer_1
  assign controlled_buffer_1_out = PC_Out ? Program_Counter_q : 8'bz;  // Controlled_Buffer controlled_buffer_2
  ROM #(.dataWidth(16)) rom_1 (.addr(Memory_Address_Register_q), .data(rom_1_data), .sel(not_2_out));
  RAM #(.dataWidth(16)) ram_1 (
    .addr(Memory_Address_Register_q), .data(rom_1_data), .sel(Memory_Address_Register_q[7]), .clk(CLK_out),
    .ld(Memory_Out), .clr(Clear));
  assign controlled_buffer_1_out = IR_Out ? Instruction_Register_q : 8'bz;  // Controlled_Buffer controlled_buffer_3
  ROM rom_2 (.addr(Instruction_Register_q_2), .data(rom_2_data));  // open: sel
  ROM rom_3 (.addr(Instruction_Register_q_2));  // open: data, sel
  ROM rom_4 (.addr(Instruction_Register_q_2));  // open: data, sel
  Clock CLK (.out(CLK_out));
  assign {controlled_buffer_4_out, controlled_buffer_1_out} = Memory_Out ? rom_1_data : 16'bz;  // Controlled_Buffer controlled_buffer_4
  assign rom_1_data = Memory_In ? {controlled_buffer_4_out, controlled_buffer_1_out} : 16'bz;  // Controlled_Buffer controlled_buffer_5
  // Probe on {controlled_buffer_4_out, controlled_buffer_1_out}
  // Probe on {controlled_buffer_4_out, controlled_buffer_1_out}
  Pull_Resistor pull_resistor_1 (.node({controlled_buffer_4_out, controlled_buffer_1_out}));
  assign controlled_buffer_1_out = Reg_A_Out ? Reg_A_q : 8'bz;  // Controlled_Buffer controlled_buffer_6
  Register Reg_A (.D(controlled_buffer_1_out), .en(Reg_A_Load), .Q(Reg_A_q), .clk(CLK_out), .clr(Clear));
  _8_Bit_ALU u_8_bit_alu_1 (
    .Output(controlled_buffer_1_out), .Input_A(Reg_A_q), .Input_B(Reg_Temp_q),
    .Carry_Borrow_Flag(n8_bit_alu_1_carry_borrow_flag[0]), .Zero_Flag(n8_bit_alu_1_carry_borrow_flag[1]),
    .EN__Enable_out(not_3_out), .DC__Decrement(decoder_2_out9), .AN__AND(decoder_2_out3),
    .XO__XOR(decoder_2_out5), .SU__Subtract(decoder_2_out2), .AD__Add(decoder_2_out1),
    .IC__Increment(decoder_2_out8), .OR__OR(decoder_2_out4), .RR__Rotate_Right(decoder_2_out6),
    .RL__Rotate_Left(decoder_2_out7));
  assign controlled_buffer_1_out = Reg_Temp_Out ? Reg_Temp_q : 8'bz;  // Controlled_Buffer controlled_buffer_7
  Register Reg_Temp (.D(controlled_buffer_1_out), .en(Reg_Temp_Load), .Q(Reg_Temp_q), .clk(CLK_out), .clr(Clear));
  assign controlled_buffer_1_out = Reg_B_Out ? Reg_B_q : 8'bz;  // Controlled_Buffer controlled_buffer_8
  Register Reg_B (.D(controlled_buffer_1_out), .en(Reg_B_Load), .Q(Reg_B_q), .clk(CLK_out), .clr(Clear));
  assign controlled_buffer_1_out = Reg_C_Out ? Reg_C_q : 8'bz;  // Controlled_Buffer controlled_buffer_9
  Register Reg_C (.D(controlled_buffer_1_out), .en(Reg_C_Load), .Q(Reg_C_q), .clk(CLK_out), .clr(Clear));
  assign controlled_buffer_1_out = SP_Out ? Stack_Pointer_q : 8'bz;  // Controlled_Buffer controlled_buffer_10
  Register Stack_Pointer (.D(controlled_buffer_1_out), .en(SP_Load), .Q(Stack_Pointer_q), .clk(CLK_out), .clr(Clear));
  Register Reg_Out (.D(controlled_buffer_1_out), .en(Reg_Out_Load), .Q(Reg_Out_q), .clk(CLK_out), .clr(Clear));
  // Probe on Reg_Out_q
  not not_3 (not_3_out, decoder_2_out0);
  Register Flags_Register (.D(n8_bit_alu_1_carry_borrow_flag), .en(Reg_F_Load), .clk(CLK_out), .clr(Clear));  // open: Q
  Decoder #(.select(4), .enable("false")) decoder_2 (
    .out0(decoder_2_out0), .out1(decoder_2_out1), .out2(decoder_2_out2), .out3(decoder_2_out3),
    .out4(decoder_2_out4), .out5(decoder_2_out5), .out6(decoder_2_out6), .out7(decoder_2_out7),
    .out8(decoder_2_out8), .out9(decoder_2_out9), .sel(ALU_Control_Word));  // open: out10, out11, out12, out13, out14, out15

  // Notes on the sheet:
  //   Microcode ROMs
  //   First 1/2 Memory ROM
  //   contents of rom_1 (hex, n*v repeats v):
  //   10e 20f 300 11*0 5 5
  //   ALU Control Word
endmodule

// ALU
module _8_Bit_ALU (
  input  [7:0] Input_A,
  input  EN__Enable_out,
  input  AD__Add,
  input  SU__Subtract,
  input  AN__AND,
  input  OR__OR,
  input  XO__XOR,
  input  RR__Rotate_Right,
  input  RL__Rotate_Left,
  input  IC__Increment,
  input  DC__Decrement,
  input  [7:0] Input_B,
  output [7:0] Output,
  output Carry_Borrow_Flag,
  output Zero_Flag
);

  wire and_1_out, and_2_out, and_3_out, and_4_out, and_5_out, and_6_out, and_7_out, and_8_out, and_9_out,
       and_10_out, and_11_out, and_12_out, and_13_out, and_14_out, and_15_out, and_16_out,
       controlled_buffer_1_out, controlled_buffer_2_out, controlled_buffer_3_out, controlled_buffer_4_out,
       controlled_buffer_5_out, controlled_buffer_6_out, controlled_buffer_7_out, controlled_buffer_8_out,
       full_adder_module_1_carry_out, full_adder_module_1_sum, full_adder_module_2_carry_out,
       full_adder_module_2_sum, full_adder_module_3_carry_out, full_adder_module_3_sum,
       full_adder_module_4_carry_out, full_adder_module_4_sum, full_adder_module_5_carry_out,
       full_adder_module_5_sum, full_adder_module_6_carry_out, full_adder_module_6_sum,
       full_adder_module_7_carry_out, full_adder_module_7_sum, full_adder_module_8_carry_out,
       full_adder_module_8_sum, or_1_out, or_2_out, or_3_out, or_4_out, or_5_out, or_6_out, or_7_out,
       or_8_out, or_9_out, or_10_out, or_11_out, or_12_out, or_13_out, xor_1_out, xor_2_out, xor_3_out,
       xor_4_out, xor_5_out, xor_6_out, xor_7_out, xor_8_out, xor_9_out, xor_10_out, xor_11_out, xor_12_out,
       xor_13_out, xor_14_out, xor_15_out, xor_16_out;

  or or_1 (or_1_out, AD__Add, SU__Subtract, IC__Increment, DC__Decrement);
  xor xor_1 (xor_1_out, or_2_out, and_1_out);
  or or_2 (or_2_out, DC__Decrement, SU__Subtract);
  or or_3 (or_3_out, SU__Subtract, IC__Increment);
  and and_1 (and_1_out, or_4_out, Input_B[7]);
  or or_4 (or_4_out, AD__Add, SU__Subtract, AN__AND, OR__OR, XO__XOR);
  xor xor_2 (xor_2_out, or_2_out, and_3_out);
  xor xor_3 (xor_3_out, or_2_out, and_2_out);
  and and_2 (and_2_out, or_4_out, Input_B[5]);
  and and_3 (and_3_out, or_4_out, Input_B[6]);
  xor xor_4 (xor_4_out, or_2_out, and_5_out);
  xor xor_5 (xor_5_out, or_2_out, and_4_out);
  and and_4 (and_4_out, or_4_out, Input_B[3]);
  and and_5 (and_5_out, or_4_out, Input_B[4]);
  xor xor_6 (xor_6_out, or_2_out, and_7_out);
  xor xor_7 (xor_7_out, or_2_out, and_6_out);
  and and_6 (and_6_out, or_4_out, Input_B[1]);
  and and_7 (and_7_out, or_4_out, Input_B[2]);
  xor xor_8 (xor_8_out, or_2_out, and_8_out);
  and and_8 (and_8_out, or_4_out, Input_B[0]);
  Full_Adder_Module full_adder_module_1 (
    .A(Input_A[0]), .B(xor_8_out), .Carry_In(or_3_out), .Sum(full_adder_module_1_sum),
    .Carry_Out(full_adder_module_1_carry_out));
  assign controlled_buffer_1_out = AN__AND ? and_9_out : 1'bz;  // Controlled_Buffer controlled_buffer_1
  and and_9 (and_9_out, Input_A[7], xor_1_out);
  assign controlled_buffer_2_out = AN__AND ? and_10_out : 1'bz;  // Controlled_Buffer controlled_buffer_2
  and and_10 (and_10_out, Input_A[6], xor_2_out);
  assign controlled_buffer_3_out = AN__AND ? and_11_out : 1'bz;  // Controlled_Buffer controlled_buffer_3
  and and_11 (and_11_out, Input_A[5], xor_3_out);
  assign controlled_buffer_4_out = AN__AND ? and_12_out : 1'bz;  // Controlled_Buffer controlled_buffer_4
  and and_12 (and_12_out, Input_A[4], xor_4_out);
  and and_13 (and_13_out, Input_A[3], xor_5_out);
  assign controlled_buffer_5_out = AN__AND ? and_13_out : 1'bz;  // Controlled_Buffer controlled_buffer_5
  assign controlled_buffer_6_out = AN__AND ? and_14_out : 1'bz;  // Controlled_Buffer controlled_buffer_6
  and and_14 (and_14_out, Input_A[2], xor_6_out);
  and and_15 (and_15_out, Input_A[1], xor_7_out);
  assign controlled_buffer_7_out = AN__AND ? and_15_out : 1'bz;  // Controlled_Buffer controlled_buffer_7
  assign controlled_buffer_8_out = AN__AND ? and_16_out : 1'bz;  // Controlled_Buffer controlled_buffer_8
  and and_16 (and_16_out, Input_A[0], xor_8_out);
  or or_5 (or_5_out, Input_A[7], xor_1_out);
  or or_6 (or_6_out, Input_A[6], xor_2_out);
  or or_7 (or_7_out, Input_A[5], xor_3_out);
  or or_8 (or_8_out, Input_A[4], xor_4_out);
  or or_9 (or_9_out, Input_A[3], xor_5_out);
  or or_10 (or_10_out, Input_A[2], xor_6_out);
  or or_11 (or_11_out, Input_A[1], xor_7_out);
  or or_12 (or_12_out, Input_A[0], xor_8_out);
  xor xor_9 (xor_9_out, Input_A[7], xor_1_out);
  xor xor_10 (xor_10_out, Input_A[6], xor_2_out);
  xor xor_11 (xor_11_out, Input_A[5], xor_3_out);
  xor xor_12 (xor_12_out, Input_A[4], xor_4_out);
  xor xor_13 (xor_13_out, Input_A[3], xor_5_out);
  xor xor_14 (xor_14_out, Input_A[2], xor_6_out);
  xor xor_15 (xor_15_out, Input_A[1], xor_7_out);
  xor xor_16 (xor_16_out, Input_A[0], xor_8_out);
  assign controlled_buffer_2_out = RR__Rotate_Right ? Input_A[7] : 1'bz;  // Controlled_Buffer controlled_buffer_9
  assign controlled_buffer_3_out = RR__Rotate_Right ? Input_A[6] : 1'bz;  // Controlled_Buffer controlled_buffer_10
  assign controlled_buffer_4_out = RR__Rotate_Right ? Input_A[5] : 1'bz;  // Controlled_Buffer controlled_buffer_11
  assign controlled_buffer_5_out = RR__Rotate_Right ? Input_A[4] : 1'bz;  // Controlled_Buffer controlled_buffer_12
  assign controlled_buffer_6_out = RR__Rotate_Right ? Input_A[3] : 1'bz;  // Controlled_Buffer controlled_buffer_13
  assign controlled_buffer_7_out = RR__Rotate_Right ? Input_A[2] : 1'bz;  // Controlled_Buffer controlled_buffer_14
  assign controlled_buffer_8_out = RR__Rotate_Right ? Input_A[1] : 1'bz;  // Controlled_Buffer controlled_buffer_15
  assign controlled_buffer_1_out = RR__Rotate_Right ? Input_A[0] : 1'bz;  // Controlled_Buffer controlled_buffer_16
  assign controlled_buffer_8_out = RL__Rotate_Left ? Input_A[7] : 1'bz;  // Controlled_Buffer controlled_buffer_17
  assign controlled_buffer_1_out = RL__Rotate_Left ? Input_A[6] : 1'bz;  // Controlled_Buffer controlled_buffer_18
  assign controlled_buffer_2_out = RL__Rotate_Left ? Input_A[5] : 1'bz;  // Controlled_Buffer controlled_buffer_19
  assign controlled_buffer_3_out = RL__Rotate_Left ? Input_A[4] : 1'bz;  // Controlled_Buffer controlled_buffer_20
  assign controlled_buffer_4_out = RL__Rotate_Left ? Input_A[3] : 1'bz;  // Controlled_Buffer controlled_buffer_21
  assign controlled_buffer_5_out = RL__Rotate_Left ? Input_A[2] : 1'bz;  // Controlled_Buffer controlled_buffer_22
  assign controlled_buffer_6_out = RL__Rotate_Left ? Input_A[1] : 1'bz;  // Controlled_Buffer controlled_buffer_23
  assign controlled_buffer_7_out = RL__Rotate_Left ? Input_A[0] : 1'bz;  // Controlled_Buffer controlled_buffer_24
  Full_Adder_Module full_adder_module_2 (
    .A(Input_A[2]), .B(xor_6_out), .Carry_In(full_adder_module_3_carry_out), .Sum(full_adder_module_2_sum),
    .Carry_Out(full_adder_module_2_carry_out));
  Full_Adder_Module full_adder_module_3 (
    .A(Input_A[1]), .B(xor_7_out), .Carry_In(full_adder_module_1_carry_out), .Sum(full_adder_module_3_sum),
    .Carry_Out(full_adder_module_3_carry_out));
  assign controlled_buffer_1_out = OR__OR ? or_5_out : 1'bz;  // Controlled_Buffer controlled_buffer_25
  assign controlled_buffer_2_out = OR__OR ? or_6_out : 1'bz;  // Controlled_Buffer controlled_buffer_26
  assign controlled_buffer_3_out = OR__OR ? or_7_out : 1'bz;  // Controlled_Buffer controlled_buffer_27
  assign controlled_buffer_4_out = OR__OR ? or_8_out : 1'bz;  // Controlled_Buffer controlled_buffer_28
  assign controlled_buffer_5_out = OR__OR ? or_9_out : 1'bz;  // Controlled_Buffer controlled_buffer_29
  assign controlled_buffer_6_out = OR__OR ? or_10_out : 1'bz;  // Controlled_Buffer controlled_buffer_30
  assign controlled_buffer_7_out = OR__OR ? or_11_out : 1'bz;  // Controlled_Buffer controlled_buffer_31
  assign controlled_buffer_8_out = OR__OR ? or_12_out : 1'bz;  // Controlled_Buffer controlled_buffer_32
  assign controlled_buffer_1_out = XO__XOR ? xor_9_out : 1'bz;  // Controlled_Buffer controlled_buffer_33
  assign controlled_buffer_2_out = XO__XOR ? xor_10_out : 1'bz;  // Controlled_Buffer controlled_buffer_34
  assign controlled_buffer_3_out = XO__XOR ? xor_11_out : 1'bz;  // Controlled_Buffer controlled_buffer_35
  assign controlled_buffer_4_out = XO__XOR ? xor_12_out : 1'bz;  // Controlled_Buffer controlled_buffer_36
  assign controlled_buffer_5_out = XO__XOR ? xor_13_out : 1'bz;  // Controlled_Buffer controlled_buffer_37
  assign controlled_buffer_6_out = XO__XOR ? xor_14_out : 1'bz;  // Controlled_Buffer controlled_buffer_38
  assign controlled_buffer_7_out = XO__XOR ? xor_15_out : 1'bz;  // Controlled_Buffer controlled_buffer_39
  assign controlled_buffer_8_out = XO__XOR ? xor_16_out : 1'bz;  // Controlled_Buffer controlled_buffer_40
  Full_Adder_Module full_adder_module_4 (
    .A(Input_A[4]), .B(xor_4_out), .Carry_In(full_adder_module_5_carry_out), .Sum(full_adder_module_4_sum),
    .Carry_Out(full_adder_module_4_carry_out));
  Full_Adder_Module full_adder_module_5 (
    .A(Input_A[3]), .B(xor_5_out), .Carry_In(full_adder_module_2_carry_out), .Sum(full_adder_module_5_sum),
    .Carry_Out(full_adder_module_5_carry_out));
  Full_Adder_Module full_adder_module_6 (
    .A(Input_A[5]), .B(xor_3_out), .Carry_In(full_adder_module_4_carry_out), .Sum(full_adder_module_6_sum),
    .Carry_Out(full_adder_module_6_carry_out));
  Full_Adder_Module full_adder_module_7 (
    .A(Input_A[7]), .B(xor_1_out), .Carry_In(full_adder_module_8_carry_out), .Sum(full_adder_module_7_sum),
    .Carry_Out(full_adder_module_7_carry_out));
  Full_Adder_Module full_adder_module_8 (
    .A(Input_A[6]), .B(xor_2_out), .Carry_In(full_adder_module_6_carry_out), .Sum(full_adder_module_8_sum),
    .Carry_Out(full_adder_module_8_carry_out));
  assign controlled_buffer_1_out = or_1_out ? full_adder_module_7_sum : 1'bz;  // Controlled_Buffer controlled_buffer_41
  assign controlled_buffer_2_out = or_1_out ? full_adder_module_8_sum : 1'bz;  // Controlled_Buffer controlled_buffer_42
  assign controlled_buffer_3_out = or_1_out ? full_adder_module_6_sum : 1'bz;  // Controlled_Buffer controlled_buffer_43
  assign controlled_buffer_4_out = or_1_out ? full_adder_module_4_sum : 1'bz;  // Controlled_Buffer controlled_buffer_44
  assign controlled_buffer_5_out = or_1_out ? full_adder_module_5_sum : 1'bz;  // Controlled_Buffer controlled_buffer_45
  assign controlled_buffer_6_out = or_1_out ? full_adder_module_2_sum : 1'bz;  // Controlled_Buffer controlled_buffer_46
  assign controlled_buffer_7_out = or_1_out ? full_adder_module_3_sum : 1'bz;  // Controlled_Buffer controlled_buffer_47
  assign controlled_buffer_8_out = or_1_out ? full_adder_module_1_sum : 1'bz;  // Controlled_Buffer controlled_buffer_48
  or or_13 (or_13_out, DC__Decrement, SU__Subtract);
  assign Output[7] = EN__Enable_out ? controlled_buffer_1_out : 1'bz;  // Controlled_Buffer controlled_buffer_49
  assign Output[6] = EN__Enable_out ? controlled_buffer_2_out : 1'bz;  // Controlled_Buffer controlled_buffer_50
  assign Output[5] = EN__Enable_out ? controlled_buffer_3_out : 1'bz;  // Controlled_Buffer controlled_buffer_51
  assign Output[4] = EN__Enable_out ? controlled_buffer_4_out : 1'bz;  // Controlled_Buffer controlled_buffer_52
  assign Output[3] = EN__Enable_out ? controlled_buffer_5_out : 1'bz;  // Controlled_Buffer controlled_buffer_53
  assign Output[2] = EN__Enable_out ? controlled_buffer_6_out : 1'bz;  // Controlled_Buffer controlled_buffer_54
  assign Output[1] = EN__Enable_out ? controlled_buffer_7_out : 1'bz;  // Controlled_Buffer controlled_buffer_55
  assign Output[0] = EN__Enable_out ? controlled_buffer_8_out : 1'bz;  // Controlled_Buffer controlled_buffer_56
  nor nor_1 (Zero_Flag, controlled_buffer_1_out, controlled_buffer_2_out, controlled_buffer_3_out, controlled_buffer_4_out, controlled_buffer_5_out, controlled_buffer_6_out, controlled_buffer_7_out, controlled_buffer_8_out);
  xor xor_17 (Carry_Borrow_Flag, or_13_out, full_adder_module_7_carry_out);

  // Notes on the sheet:
  //   Bus Output
endmodule

module Full_Adder_Module (
  input  A,
  input  B,
  input  Carry_In,
  output Sum,
  output Carry_Out
);

  wire and_1_out, and_2_out, xor_1_out;

  xor xor_1 (xor_1_out, A, B);
  and and_1 (and_1_out, A, B);
  xor xor_2 (Sum, xor_1_out, Carry_In);
  and and_2 (and_2_out, xor_1_out, Carry_In);
  or or_1 (Carry_Out, and_2_out, and_1_out);
endmodule

module _8_Bit_Register (
  input  CLK,
  input  [7:0] D,
  input  Enable,
  input  RST,
  output [7:0] Q
);

  D_Flip_Flop d_ff_1 (.clk(CLK), .D(D[0]), .Q(Q[0]), .en(Enable), .reset(RST));  // open: Qn, preset
  D_Flip_Flop d_ff_2 (.clk(CLK), .D(D[1]), .Q(Q[1]), .en(Enable), .reset(RST));  // open: Qn, preset
  D_Flip_Flop d_ff_3 (.clk(CLK), .D(D[2]), .Q(Q[2]), .en(Enable), .reset(RST));  // open: Qn, preset
  D_Flip_Flop d_ff_4 (.clk(CLK), .D(D[3]), .Q(Q[3]), .en(Enable), .reset(RST));  // open: Qn, preset
  D_Flip_Flop d_ff_5 (.clk(CLK), .D(D[4]), .Q(Q[4]), .en(Enable), .reset(RST));  // open: Qn, preset
  D_Flip_Flop d_ff_6 (.clk(CLK), .D(D[5]), .Q(Q[5]), .en(Enable), .reset(RST));  // open: Qn, preset
  D_Flip_Flop d_ff_7 (.clk(CLK), .D(D[6]), .Q(Q[6]), .en(Enable), .reset(RST));  // open: Qn, preset
  D_Flip_Flop d_ff_8 (.clk(CLK), .D(D[7]), .Q(Q[7]), .en(Enable), .reset(RST));  // open: Qn, preset
endmodule
